# Fritzing sketch pdbms_cuicit (saved by Fritzing 0.9.3b)

parts:
  Squix1 = OLED 0.96" 128x64 I2C SSD1306
  Part1 = BH1750
  Load_Cell1 = Load Cell - Red/white/black/green
  Part2 = HX711 Weighing Sensor Module
  U1 = NodeMCU V3.0
  Part3 = FC-28 Soil Hygrometer Module
  Part4 = FC-28 Soil Hygrometer Module - Probe
  DHT1 = DHT22 Humidity and Temperature Sensor

nets:
  VCC: Squix1.VCC, Part1.VCC
  GND: Squix1.GND, Part1.GND
  N1: Squix1.SCL, U1.D1
  N2: Squix1.SCA, U1.D2
  N3: Load_Cell1.wire1, Part2.E+
  N4: Load_Cell1.wire2, Part2.A+
  N5: Load_Cell1.wire3, Part2.E-
  N6: Load_Cell1.wire4, Part2.A-
  N7: Part2.VCC, U1.VU
  N8: Part2.GND, U1.GND#41
  N9: Part2.DO/RX, U1.D3
  N10: Part2.CK/TX, U1.D4
  N11: U1.D5, DHT1.DATA
  N12: U1.A0, Part3.AO
  N13: Part3.POS, Part4.POS
  N14: Part3.NEG, Part4.NEG

custom parts:
  BH1750: Light Sensor
  Load Cell - Red/white/black/green: A rectangle load cell/weighting pressure Sensor with four wires - Red, white, black, green. Normally corresponding with E+, E-, A+, A- respectively.
  NodeMCU V3.0: ESP8266 based NodeMCU
  FC-28 Soil Hygrometer Module: The FC-28 is a soil hygrometer module that uses the Texas Instruments LM393 comparator chip to provide an analog measurement of soil humidity. The digital output is high when soil moisture is over a certain threshold, as determined by adjusting the potentiometer.
  FC-28 Soil Hygrometer Module - Probe: The FC-28 is a soil hygrometer module that uses the Texas Instruments LM393 comparator chip to provide an analog measurement of soil humidity.
